# Fritzing sketch robot arm (saved by Fritzing 0.9.3b)
breadboards: 1

parts:
  U1 = ESP8266 NodeMCU LoLin base
  J3 = Basic Servo
  J4 = Basic Servo
  J5 = Basic Servo
  J2 = Basic Servo

nets:
  GND: U1.GND1-0, U1.GND3-2, U1.GND8-9, U1.GND8-10, J3.gnd, J4.gnd, J5.gnd, J2.gnd
  VCC: U1.3V1-0, U1.3V3-2, J3.vcc, J4.vcc, J5.vcc, J2.vcc
  N1: U1.D1-0, U1.D1-3, J4.pulse
  N2: U1.D2-0, J2.pulse
  N3: U1.D4-0, U1.D4-3, J3.pulse
  N4: U1.D5-0, J5.pulse

custom parts:
  ESP8266 NodeMCU LoLin base: ESP8266 based NodeMCU Base
